// Logisim project projetoTesteMult.circ as structural Verilog: 16 circuits, main circuit main
module soma (
  input  a,
  input  b,
  input  c,
  output s,
  output r
);

  wire and_1_out, and_2_out, and_3_out, and_4_out, and_5_out, and_6_out, and_7_out, not_1_out, not_2_out,
       not_3_out, not_4_out, not_5_out, not_6_out;

  not not_1 (not_1_out, a);
  not not_2 (not_2_out, b);
  not not_3 (not_3_out, a);
  not not_4 (not_4_out, c);
  not not_5 (not_5_out, b);
  not not_6 (not_6_out, c);
  and and_1 (and_1_out, b, c);
  and and_2 (and_2_out, a, c);
  and and_3 (and_3_out, a, b);
  and and_4 (and_4_out, not_1_out, not_2_out, c);
  and and_5 (and_5_out, not_3_out, b, not_4_out);
  and and_6 (and_6_out, a, not_5_out, not_6_out);
  and and_7 (and_7_out, a, b, c);
  or or_1 (r, and_1_out, and_2_out, and_3_out);
  or or_2 (s, and_4_out, and_5_out, and_6_out, and_7_out);
endmodule

module somador (
  input  in_1,
  input  in_2,
  input  in_3,
  input  in_4,
  input  in_5,
  input  in_6,
  input  in_7,
  input  in_8,
  output out_9,
  output out_10,
  output out_11,
  output out_12,
  output out_13
);

  wire soma_1_r, soma_2_r, soma_3_r;

  soma soma_1 (.a(in_1), .b(in_5), .c(1'b0), .s(out_9), .r(soma_1_r));
  soma soma_2 (.a(in_2), .b(in_6), .c(soma_1_r), .s(out_10), .r(soma_2_r));
  soma soma_3 (.a(in_3), .b(in_7), .c(soma_2_r), .s(out_11), .r(soma_3_r));
  soma soma_4 (.a(in_4), .b(in_8), .c(soma_3_r), .s(out_12), .r(out_13));
endmodule

module main (
  input  in_1,
  input  in_2,
  input  F,
  input  G,
  input  A,
  input  B,
  input  E,
  input  D,
  input  C,
  input  F_2,
  input  G_2,
  input  A_2,
  input  B_2,
  input  E_2,
  input  D_2,
  input  C_2,
  output NUM1___NUM2,
  output NUM2___NUM2,
  output NUM1___NUM2_2
);

  wire calculador_seletor_1_error, calculador_seletor_1_null, calculador_seletor_1_out_11,
       calculador_seletor_1_out_12, calculador_seletor_1_out_13, calculador_seletor_1_out_14,
       calculador_seletor_1_out_17, calculador_seletor_1_out_18, calculador_seletor_1_out_19,
       calculador_seletor_1_out_20, conversor_bin_dec_1_a, conversor_bin_dec_1_b, conversor_bin_dec_1_c,
       conversor_bin_dec_1_d, conversor_bin_dec_1_e, conversor_bin_dec_1_f, conversor_bin_dec_1_g,
       conversor_dec_bin_1_e_2, conversor_dec_bin_1_h, conversor_dec_bin_1_i, conversor_dec_bin_1_j,
       conversor_dec_bin_1_k, conversor_dec_bin_2_e_2, conversor_dec_bin_2_h, conversor_dec_bin_2_i,
       conversor_dec_bin_2_j, conversor_dec_bin_2_k, or_1_out;

  _7_Segment_Display u_7_segment_display_1 (.g(F), .f(G), .a(A), .b(B), .e(E), .d(D), .c(C));  // open: dp
  _7_Segment_Display u_7_segment_display_2 (.g(F_2), .f(G_2), .a(A_2), .b(B_2), .e(E_2), .d(D_2), .c(C_2));  // open: dp
  conversor__dec___bin conversor_dec_bin_1 (
    .a(A), .b(B), .c(C), .d(D), .e(E), .f(F), .g(G), .h(conversor_dec_bin_1_h), .i(conversor_dec_bin_1_i),
    .j(conversor_dec_bin_1_j), .k(conversor_dec_bin_1_k), .E_2(conversor_dec_bin_1_e_2));
  conversor__dec___bin conversor_dec_bin_2 (
    .a(A_2), .b(B_2), .c(C_2), .d(D_2), .e(E_2), .f(F_2), .g(G_2), .h(conversor_dec_bin_2_h),
    .i(conversor_dec_bin_2_i), .j(conversor_dec_bin_2_j), .k(conversor_dec_bin_2_k),
    .E_2(conversor_dec_bin_2_e_2));
  or or_1 (or_1_out, conversor_dec_bin_2_e_2, conversor_dec_bin_1_e_2, calculador_seletor_1_null);
  calculador_seletor calculador_seletor_1 (
    .in_3(conversor_dec_bin_1_k), .in_4(conversor_dec_bin_1_j), .in_5(conversor_dec_bin_1_i),
    .in_6(conversor_dec_bin_1_h), .in_7(conversor_dec_bin_2_k), .in_8(conversor_dec_bin_2_j),
    .in_9(conversor_dec_bin_2_i), .in_10(conversor_dec_bin_2_h), .in_1(in_1), .in_2(in_2),
    .error(calculador_seletor_1_error), .\null (calculador_seletor_1_null),
    .out_11(calculador_seletor_1_out_11), .out_12(calculador_seletor_1_out_12),
    .out_13(calculador_seletor_1_out_13), .out_14(calculador_seletor_1_out_14),
    .out_17(calculador_seletor_1_out_17), .out_18(calculador_seletor_1_out_18),
    .out_19(calculador_seletor_1_out_19), .out_20(calculador_seletor_1_out_20));
  conversor__bin___dec conversor_bin_dec_1 (
    .\null (or_1_out), .x1(calculador_seletor_1_out_14), .x2(calculador_seletor_1_out_13),
    .x3(calculador_seletor_1_out_12), .x4(calculador_seletor_1_out_11), .a(conversor_bin_dec_1_a),
    .b(conversor_bin_dec_1_b), .c(conversor_bin_dec_1_c), .d(conversor_bin_dec_1_d),
    .e(conversor_bin_dec_1_e), .f(conversor_bin_dec_1_f), .g(conversor_bin_dec_1_g));
  _7_Segment_Display u_7_segment_display_3 (
    .g(conversor_bin_dec_1_f), .f(conversor_bin_dec_1_g), .a(conversor_bin_dec_1_a),
    .b(conversor_bin_dec_1_b), .e(conversor_bin_dec_1_e), .d(conversor_bin_dec_1_d), .c(conversor_bin_dec_1_c));  // open: dp
  _7_Segment_Display u_7_segment_display_4 (.g(calculador_seletor_1_out_20));  // open: f, a, b, e, d, c, dp
  _7_Segment_Display u_7_segment_display_5 (
    .g(calculador_seletor_1_error), .f(calculador_seletor_1_error), .a(calculador_seletor_1_error),
    .e(calculador_seletor_1_error), .d(calculador_seletor_1_error));  // open: b, c, dp
  _7_Segment_Display u_7_segment_display_6 (
    .f(calculador_seletor_1_error), .a(calculador_seletor_1_error), .e(calculador_seletor_1_error));  // open: g, b, d, c, dp
  comparador_erro comparador_erro_1 (
    .\null (or_1_out), .x1MAx2(calculador_seletor_1_out_17), .x1IGUx2(calculador_seletor_1_out_18),
    .x1MEx2(calculador_seletor_1_out_19), .x1MAx2_2(NUM1___NUM2_2), .x1IGUx2_2(NUM2___NUM2),
    .x1MEx2_2(NUM1___NUM2));
  _7_Segment_Display u_7_segment_display_7 (
    .f(calculador_seletor_1_error), .a(calculador_seletor_1_error), .e(calculador_seletor_1_error));  // open: g, b, d, c, dp
  _7_Segment_Display u_7_segment_display_8 (
    .f(calculador_seletor_1_error), .a(calculador_seletor_1_error), .b(calculador_seletor_1_error),
    .e(calculador_seletor_1_error), .d(calculador_seletor_1_error), .c(calculador_seletor_1_error));  // open: g, dp
endmodule

module conversor__dec___bin (
  input  a,
  input  b,
  input  c,
  input  d,
  input  e,
  input  f,
  input  g,
  output h,
  output i,
  output j,
  output k,
  output E_2
);

  wire and_1_out, and_2_out, and_3_out, and_4_out, and_5_out, and_6_out, and_7_out, and_8_out, and_9_out,
       and_10_out, and_11_out, and_12_out, and_13_out, and_14_out, and_15_out, and_16_out, and_17_out,
       and_18_out, and_19_out, and_20_out, and_21_out, and_22_out, and_23_out, and_24_out, and_25_out,
       and_26_out, and_27_out, and_28_out, and_29_out, and_30_out, and_31_out, and_32_out, and_33_out,
       and_34_out, and_35_out, and_36_out, and_37_out, and_38_out, and_39_out, and_40_out, not_1_out,
       not_2_out, not_3_out, not_4_out, not_5_out, not_6_out, not_7_out, not_8_out, not_9_out, not_10_out,
       not_11_out, not_12_out, not_13_out, not_14_out, not_15_out, not_16_out, not_17_out, not_18_out,
       not_19_out, not_20_out, not_21_out, not_22_out, not_23_out, not_24_out, not_25_out, not_26_out,
       not_27_out, not_28_out, not_29_out, not_30_out, not_31_out, not_32_out, not_33_out, not_34_out,
       not_35_out, not_36_out, not_37_out, not_38_out, not_39_out, not_40_out, not_41_out, not_42_out,
       not_43_out, not_44_out, not_45_out, not_46_out, not_47_out, not_48_out, not_49_out, not_50_out,
       not_51_out, not_52_out, not_53_out, not_54_out, not_55_out, not_56_out, not_57_out, not_58_out,
       not_59_out, not_60_out, not_61_out, not_62_out, not_63_out, not_64_out, not_65_out, not_66_out,
       not_67_out, not_68_out, not_69_out, not_70_out, not_71_out, not_72_out, not_73_out, not_74_out,
       not_75_out, not_76_out, not_77_out;

  not not_1 (not_1_out, a);
  not not_2 (not_2_out, b);
  not not_3 (not_3_out, a);
  not not_4 (not_4_out, g);
  not not_5 (not_5_out, b);
  not not_6 (not_6_out, c);
  not not_7 (not_7_out, b);
  not not_8 (not_8_out, c);
  not not_9 (not_9_out, d);
  not not_10 (not_10_out, e);
  not not_11 (not_11_out, g);
  not not_12 (not_12_out, a);
  not not_13 (not_13_out, d);
  not not_14 (not_14_out, e);
  not not_15 (not_15_out, a);
  not not_16 (not_16_out, g);
  not not_17 (not_17_out, b);
  not not_18 (not_18_out, c);
  not not_19 (not_19_out, b);
  not not_20 (not_20_out, c);
  not not_21 (not_21_out, b);
  not not_22 (not_22_out, d);
  not not_23 (not_23_out, e);
  not not_24 (not_24_out, g);
  not not_25 (not_25_out, b);
  not not_26 (not_26_out, b);
  not not_27 (not_27_out, c);
  not not_28 (not_28_out, c);
  not not_29 (not_29_out, g);
  not not_30 (not_30_out, d);
  not not_31 (not_31_out, e);
  not not_32 (not_32_out, g);
  not not_33 (not_33_out, e);
  not not_34 (not_34_out, g);
  not not_35 (not_35_out, d);
  not not_36 (not_36_out, a);
  not not_37 (not_37_out, b);
  not not_38 (not_38_out, d);
  not not_39 (not_39_out, e);
  not not_40 (not_40_out, f);
  not not_41 (not_41_out, g);
  not not_42 (not_42_out, a);
  not not_43 (not_43_out, g);
  not not_44 (not_44_out, b);
  not not_45 (not_45_out, c);
  not not_46 (not_46_out, d);
  not not_47 (not_47_out, e);
  not not_48 (not_48_out, e);
  not not_49 (not_49_out, g);
  not not_50 (not_50_out, a);
  not not_51 (not_51_out, c);
  not not_52 (not_52_out, b);
  not not_53 (not_53_out, g);
  not not_54 (not_54_out, c);
  not not_55 (not_55_out, e);
  not not_56 (not_56_out, e);
  not not_57 (not_57_out, f);
  not not_58 (not_58_out, a);
  not not_59 (not_59_out, d);
  not not_60 (not_60_out, g);
  not not_61 (not_61_out, d);
  not not_62 (not_62_out, f);
  not not_63 (not_63_out, d);
  not not_64 (not_64_out, g);
  not not_65 (not_65_out, a);
  not not_66 (not_66_out, e);
  not not_67 (not_67_out, f);
  not not_68 (not_68_out, g);
  not not_69 (not_69_out, b);
  not not_70 (not_70_out, d);
  not not_71 (not_71_out, b);
  not not_72 (not_72_out, f);
  not not_73 (not_73_out, c);
  not not_74 (not_74_out, a);
  not not_75 (not_75_out, d);
  not not_76 (not_76_out, e);
  not not_77 (not_77_out, g);
  and and_1 (and_1_out, not_1_out, not_2_out, c, d, e, f, g);
  and and_2 (and_2_out, not_3_out, b, c, d, e, f, not_4_out);
  and and_3 (and_3_out, a, not_5_out, not_6_out, e, f, g);
  and and_4 (and_4_out, a, not_7_out, not_8_out, d, e, g);
  and and_5 (and_5_out, a, b, c, not_9_out, not_10_out, f, not_11_out);
  and and_6 (and_6_out, a, b, c, e, f, g);
  and and_7 (and_7_out, a, b, c, d, f, g);
  and and_8 (and_8_out, not_12_out, b, c, not_13_out, not_14_out, f, g);
  and and_9 (and_9_out, not_15_out, b, c, d, e, f, not_16_out);
  and and_10 (and_10_out, a, not_17_out, not_18_out, e, f, g);
  and and_11 (and_11_out, a, not_19_out, not_20_out, d, e, g);
  and and_12 (and_12_out, a, not_21_out, c, d, f, g);
  and and_13 (and_13_out, a, b, c, not_22_out, not_23_out, not_24_out);
  and and_14 (and_14_out, not_25_out, c, d, e, f, g);
  and and_15 (and_15_out, a, not_26_out, not_27_out, e, f, g);
  and and_16 (and_16_out, a, b, not_28_out, d, e, f, not_29_out);
  and and_17 (and_17_out, a, b, c, not_30_out, not_31_out, not_32_out);
  and and_18 (and_18_out, a, b, c, not_33_out, f, not_34_out);
  and and_19 (and_19_out, a, b, c, not_35_out, e, f, g);
  and and_20 (and_20_out, not_36_out, not_37_out, c, d, e, f, g);
  and and_21 (and_21_out, b, c, not_38_out, not_39_out, not_40_out, not_41_out);
  and and_22 (and_22_out, not_42_out, b, c, d, e, f, not_43_out);
  and and_23 (and_23_out, a, not_44_out, not_45_out, not_46_out, e, f, g);
  and and_24 (and_24_out, a, c, d, not_47_out, f, g);
  and and_25 (and_25_out, a, b, c, not_48_out, f, not_49_out);
  and and_26 (and_26_out, not_50_out, not_51_out);
  and and_27 (and_27_out, not_52_out, not_53_out);
  and and_28 (and_28_out, not_54_out, not_55_out);
  and and_29 (and_29_out, not_56_out, not_57_out, g);
  and and_30 (and_30_out, not_58_out, not_59_out, f, not_60_out);
  and and_31 (and_31_out, not_61_out, e, not_62_out);
  and and_32 (and_32_out, not_63_out, e, not_64_out);
  and and_33 (and_33_out, not_65_out, d, not_66_out);
  and and_34 (and_34_out, d, not_67_out, not_68_out);
  and and_35 (and_35_out, not_69_out, c, not_70_out);
  and and_36 (and_36_out, not_71_out, c, not_72_out);
  and and_37 (and_37_out, b, not_73_out, g);
  and and_38 (and_38_out, not_74_out, b, e, g);
  and and_39 (and_39_out, a, not_75_out, not_76_out, g);
  and and_40 (and_40_out, a, c, e, not_77_out);
  or or_1 (h, and_1_out, and_2_out, and_3_out, and_4_out, and_5_out, and_6_out, and_7_out);
  or or_2 (i, and_8_out, and_9_out, and_10_out, and_11_out, and_12_out, and_13_out);
  or or_3 (j, and_14_out, and_15_out, and_16_out, and_17_out, and_18_out, and_19_out);
  or or_4 (k, and_20_out, and_21_out, and_22_out, and_23_out, and_24_out, and_25_out);
  or or_5 (E_2, and_26_out, and_27_out, and_28_out, and_29_out, and_30_out, and_31_out, and_32_out, and_33_out, and_34_out, and_35_out, and_36_out, and_37_out, and_38_out, and_39_out, and_40_out);
endmodule

module conversor__bin___dec (
  input  \null ,
  input  x1,
  input  x2,
  input  x3,
  input  x4,
  output a,
  output b,
  output c,
  output d,
  output e,
  output f,
  output g
);

  wire and_1_out, and_2_out, and_3_out, and_4_out, and_5_out, and_6_out, and_7_out, and_8_out, and_9_out,
       and_10_out, and_11_out, and_12_out, and_13_out, and_14_out, and_15_out, and_16_out, and_17_out,
       and_18_out, and_19_out, and_20_out, and_21_out, and_22_out, and_23_out, and_24_out, and_25_out,
       and_26_out, and_27_out, and_28_out, and_29_out, and_30_out, and_31_out, and_32_out, and_33_out,
       and_34_out, and_35_out, not_1_out, not_2_out, not_3_out, not_4_out, not_5_out, not_6_out, not_7_out,
       not_8_out, not_9_out, not_10_out, not_11_out, not_12_out, not_13_out, not_14_out, not_15_out,
       not_16_out, not_17_out, not_18_out, not_19_out, not_20_out, not_21_out, not_22_out, not_23_out,
       not_24_out, not_25_out, not_26_out, not_27_out, not_28_out, not_29_out, not_30_out, not_31_out,
       not_32_out, not_33_out, not_34_out, not_35_out, not_36_out, not_37_out, not_38_out, not_39_out,
       not_40_out, not_41_out, not_42_out, not_43_out, not_44_out, not_45_out, not_46_out, not_47_out,
       not_48_out, not_49_out, not_50_out, not_51_out, not_52_out, not_53_out, not_54_out, not_55_out,
       not_56_out, not_57_out, not_58_out, not_59_out, not_60_out, not_61_out, not_62_out, not_63_out,
       not_64_out, not_65_out, not_66_out, not_67_out, not_68_out, not_69_out, not_70_out, not_71_out,
       not_72_out, not_73_out, not_74_out, not_75_out, not_76_out, not_77_out, not_78_out, not_79_out;

  not not_1 (not_1_out, \null );
  not not_2 (not_2_out, x2);
  not not_3 (not_3_out, x4);
  not not_4 (not_4_out, \null );
  not not_5 (not_5_out, x1);
  not not_6 (not_6_out, \null );
  not not_7 (not_7_out, x1);
  not not_8 (not_8_out, \null );
  not not_9 (not_9_out, \null );
  not not_10 (not_10_out, x2);
  not not_11 (not_11_out, x3);
  not not_12 (not_12_out, \null );
  not not_13 (not_13_out, x4);
  not not_14 (not_14_out, \null );
  not not_15 (not_15_out, x1);
  not not_16 (not_16_out, x2);
  not not_17 (not_17_out, \null );
  not not_18 (not_18_out, x1);
  not not_19 (not_19_out, x3);
  not not_20 (not_20_out, x4);
  not not_21 (not_21_out, \null );
  not not_22 (not_22_out, x2);
  not not_23 (not_23_out, x4);
  not not_24 (not_24_out, \null );
  not not_25 (not_25_out, x1);
  not not_26 (not_26_out, \null );
  not not_27 (not_27_out, x3);
  not not_28 (not_28_out, \null );
  not not_29 (not_29_out, x1);
  not not_30 (not_30_out, x3);
  not not_31 (not_31_out, \null );
  not not_32 (not_32_out, x1);
  not not_33 (not_33_out, \null );
  not not_34 (not_34_out, x3);
  not not_35 (not_35_out, \null );
  not not_36 (not_36_out, x1);
  not not_37 (not_37_out, \null );
  not not_38 (not_38_out, x2);
  not not_39 (not_39_out, \null );
  not not_40 (not_40_out, x1);
  not not_41 (not_41_out, x2);
  not not_42 (not_42_out, x4);
  not not_43 (not_43_out, \null );
  not not_44 (not_44_out, x2);
  not not_45 (not_45_out, \null );
  not not_46 (not_46_out, x3);
  not not_47 (not_47_out, \null );
  not not_48 (not_48_out, x4);
  not not_49 (not_49_out, \null );
  not not_50 (not_50_out, x3);
  not not_51 (not_51_out, x4);
  not not_52 (not_52_out, \null );
  not not_53 (not_53_out, x2);
  not not_54 (not_54_out, x4);
  not not_55 (not_55_out, \null );
  not not_56 (not_56_out, x4);
  not not_57 (not_57_out, \null );
  not not_58 (not_58_out, \null );
  not not_59 (not_59_out, \null );
  not not_60 (not_60_out, x2);
  not not_61 (not_61_out, \null );
  not not_62 (not_62_out, x4);
  not not_63 (not_63_out, \null );
  not not_64 (not_64_out, x1);
  not not_65 (not_65_out, x3);
  not not_66 (not_66_out, \null );
  not not_67 (not_67_out, x2);
  not not_68 (not_68_out, \null );
  not not_69 (not_69_out, \null );
  not not_70 (not_70_out, x3);
  not not_71 (not_71_out, x4);
  not not_72 (not_72_out, \null );
  not not_73 (not_73_out, x1);
  not not_74 (not_74_out, x3);
  not not_75 (not_75_out, \null );
  not not_76 (not_76_out, x4);
  not not_77 (not_77_out, \null );
  not not_78 (not_78_out, x2);
  not not_79 (not_79_out, \null );
  and and_1 (and_1_out, not_1_out, not_2_out, not_3_out);
  and and_2 (and_2_out, not_4_out, not_5_out, x3);
  and and_3 (and_3_out, not_6_out, not_7_out, x2, x4);
  and and_4 (and_4_out, not_8_out, x2, x3);
  and and_5 (and_5_out, not_9_out, x1, not_10_out, not_11_out);
  and and_6 (and_6_out, not_12_out, x1, not_13_out);
  and and_7 (and_7_out, not_14_out, not_15_out, not_16_out);
  and and_8 (and_8_out, not_17_out, not_18_out, not_19_out, not_20_out);
  and and_9 (and_9_out, not_21_out, not_22_out, not_23_out);
  and and_10 (and_10_out, not_24_out, not_25_out, x3, x4);
  and and_11 (and_11_out, not_26_out, x1, not_27_out, x4);
  and and_12 (and_12_out, not_28_out, not_29_out, not_30_out);
  and and_13 (and_13_out, not_31_out, not_32_out, x4);
  and and_14 (and_14_out, not_33_out, not_34_out, x4);
  and and_15 (and_15_out, not_35_out, not_36_out, x2);
  and and_16 (and_16_out, not_37_out, x1, not_38_out);
  and and_17 (and_17_out, not_39_out, not_40_out, not_41_out, not_42_out);
  and and_18 (and_18_out, not_43_out, not_44_out, x3, x4);
  and and_19 (and_19_out, not_45_out, x2, not_46_out, x4);
  and and_20 (and_20_out, not_47_out, x2, x3, not_48_out);
  and and_21 (and_21_out, not_49_out, x1, not_50_out, not_51_out);
  and and_22 (and_22_out, not_52_out, not_53_out, not_54_out);
  and and_23 (and_23_out, not_55_out, x3, not_56_out);
  and and_24 (and_24_out, not_57_out, x1, x3);
  and and_25 (and_25_out, not_58_out, x1, x2);
  and and_26 (and_26_out, not_59_out, not_60_out, x3);
  and and_27 (and_27_out, not_61_out, x3, not_62_out);
  and and_28 (and_28_out, not_63_out, not_64_out, x2, not_65_out);
  and and_29 (and_29_out, not_66_out, x1, not_67_out);
  and and_30 (and_30_out, not_68_out, x1, x4);
  and and_31 (and_31_out, not_69_out, not_70_out, not_71_out);
  and and_32 (and_32_out, not_72_out, not_73_out, x2, not_74_out);
  and and_33 (and_33_out, not_75_out, x2, not_76_out);
  and and_34 (and_34_out, not_77_out, x1, not_78_out);
  and and_35 (and_35_out, not_79_out, x1, x3);
  or or_1 (a, and_1_out, and_2_out, and_3_out, and_4_out, and_5_out, and_6_out);
  or or_2 (b, and_7_out, and_8_out, and_9_out, and_10_out, and_11_out);
  or or_3 (c, and_12_out, and_13_out, and_14_out, and_15_out, and_16_out);
  or or_4 (d, and_17_out, and_18_out, and_19_out, and_20_out, and_21_out);
  or or_5 (e, and_22_out, and_23_out, and_24_out, and_25_out);
  or or_6 (f, and_26_out, and_27_out, and_28_out, and_29_out, and_30_out);
  or or_7 (g, and_31_out, and_32_out, and_33_out, and_34_out, and_35_out);
endmodule

module calculador_seletor (
  input  in_1,
  input  in_2,
  input  in_3,
  input  in_4,
  input  in_5,
  input  in_6,
  input  in_7,
  input  in_8,
  input  in_9,
  input  in_10,
  output out_11,
  output out_12,
  output out_13,
  output out_14,
  output error,
  output \null ,
  output out_17,
  output out_18,
  output out_19,
  output out_20
);

  wire and_2_out, Mult1_a, Mult1_b, Mult1_c, Mult1_d, Multi2_a, Multi2_b, Multi2_c, Multi2_d, Multi2_null,
       Multi3_a, Multi3_b, Multi3_c, Multi3_d, Multi3_null, Multi4_a, Multi4_b, Multi4_c, Multi4_d,
       Multi4_null, not_1_out, or_1_out, seletor_1_null, seletor_2_null, seletor_3_null, seletor_4_null,
       Soma_2_out_9, Soma_2_out_10, Soma_2_out_11, Soma_2_out_12, Soma_2_out_13, Soma_3_out_9, Soma_3_out_10,
       Soma_3_out_11, Soma_3_out_12, Soma_3_out_13, Soma_4_out_9, Soma_4_out_10, Soma_4_out_11,
       Soma_4_out_12, Soma_4_out_13, Soma_5_out_9, Soma_5_out_10, Soma_5_out_11, Soma_5_out_12,
       Soma_5_out_13, Soma_out_9, Soma_out_10, Soma_out_11, Soma_out_12, Soma_out_13, Sub_a, Sub_b, Sub_c,
       Sub_d, subtrador_inv_1_a, subtrador_inv_1_b, subtrador_inv_1_c, subtrador_inv_1_d, subtrador_inv_1_neg;

  multiplicador_um Mult1 (
    .x1(in_7), .x2(in_6), .x3(in_5), .x4(in_4), .x5(in_3), .a(Mult1_a), .b(Mult1_b), .c(Mult1_c), .d(Mult1_d));
  multiplicador_dois Multi2 (
    .x1(in_8), .x2(in_6), .x3(in_5), .x4(in_4), .x5(in_3), .a(Multi2_a), .b(Multi2_b), .c(Multi2_c),
    .d(Multi2_d), .\null (Multi2_null));
  multiplicador_tres Multi3 (
    .x1(in_9), .x2(in_6), .x3(in_5), .x4(in_4), .x5(in_3), .a(Multi3_a), .b(Multi3_b), .c(Multi3_c),
    .d(Multi3_d), .\null (Multi3_null));
  multiplicador_quatro Multi4 (
    .x1(in_10), .x2(in_6), .x3(in_5), .x4(in_4), .x5(in_3), .a(Multi4_a), .b(Multi4_b), .c(Multi4_c),
    .d(Multi4_d), .\null (Multi4_null));
  subtrador Sub (.x1(in_10), .x2(in_9), .x3(in_8), .x4(in_7), .a(Sub_a), .b(Sub_b), .c(Sub_c), .d(Sub_d));
  somador Soma (
    .in_1(Mult1_a), .in_2(Mult1_b), .in_3(Mult1_c), .in_4(Mult1_d), .in_5(Multi2_a), .in_6(Multi2_b),
    .in_7(Multi2_c), .in_8(Multi2_d), .out_13(Soma_out_13), .out_9(Soma_out_9), .out_10(Soma_out_10),
    .out_11(Soma_out_11), .out_12(Soma_out_12));
  somador Soma_2 (
    .in_1(Multi3_a), .in_2(Multi3_b), .in_3(Multi3_c), .in_4(Multi3_d), .in_5(Multi4_a), .in_6(Multi4_b),
    .in_7(Multi4_c), .in_8(Multi4_d), .out_13(Soma_2_out_13), .out_9(Soma_2_out_9), .out_10(Soma_2_out_10),
    .out_11(Soma_2_out_11), .out_12(Soma_2_out_12));
  or or_1 (or_1_out, Multi2_null, Multi3_null, Multi4_null, Soma_2_out_13, Soma_out_13, Soma_5_out_13);
  somador Soma_3 (
    .in_1(in_3), .in_2(in_4), .in_3(in_5), .in_4(in_6), .in_5(in_7), .in_6(in_8), .in_7(in_9), .in_8(in_10),
    .out_13(Soma_3_out_13), .out_9(Soma_3_out_9), .out_10(Soma_3_out_10), .out_11(Soma_3_out_11),
    .out_12(Soma_3_out_12));
  somador Soma_4 (
    .in_1(in_3), .in_2(in_4), .in_3(in_5), .in_4(in_6), .in_5(Sub_a), .in_6(Sub_b), .in_7(Sub_c),
    .in_8(Sub_d), .out_13(Soma_4_out_13), .out_9(Soma_4_out_9), .out_10(Soma_4_out_10),
    .out_11(Soma_4_out_11), .out_12(Soma_4_out_12));
  somador Soma_5 (
    .in_1(Soma_out_9), .in_2(Soma_out_10), .in_3(Soma_out_11), .in_4(Soma_out_12), .in_5(Soma_2_out_9),
    .in_6(Soma_2_out_10), .in_7(Soma_2_out_11), .in_8(Soma_2_out_12), .out_13(Soma_5_out_13),
    .out_9(Soma_5_out_9), .out_10(Soma_5_out_10), .out_11(Soma_5_out_11), .out_12(Soma_5_out_12));
  subtrador_inv subtrador_inv_1 (
    .cond(out_19), .x1(Soma_4_out_12), .x2(Soma_4_out_11), .x3(Soma_4_out_10), .x4(Soma_4_out_9),
    .neg(subtrador_inv_1_neg), .a(subtrador_inv_1_a), .b(subtrador_inv_1_b), .c(subtrador_inv_1_c),
    .d(subtrador_inv_1_d));
  comparador comparador_1 (
    .x1(Soma_4_out_13), .x2(Soma_4_out_12), .x3(Soma_4_out_11), .x4(Soma_4_out_10), .x5(Soma_4_out_9),
    .a(out_17), .b(out_18), .c(out_19));
  and and_1 (out_20, subtrador_inv_1_neg, and_2_out);
  seletor seletor_1 (
    .soma1(Soma_3_out_9), .sub1(subtrador_inv_1_d), .mult1(Soma_5_out_9), .s1(in_1), .s2(in_2),
    .bit1(out_11), .\null (seletor_1_null));
  not not_1 (not_1_out, in_1);
  seletor seletor_2 (
    .soma1(Soma_3_out_10), .sub1(subtrador_inv_1_c), .mult1(Soma_5_out_10), .s1(in_1), .s2(in_2),
    .bit1(out_12), .\null (seletor_2_null));
  and and_2 (and_2_out, not_1_out, in_2);
  seletor seletor_3 (
    .soma1(Soma_3_out_11), .sub1(subtrador_inv_1_b), .mult1(Soma_5_out_11), .s1(in_1), .s2(in_2),
    .bit1(out_13), .\null (seletor_3_null));
  seletor seletor_4 (
    .soma1(Soma_3_out_12), .sub1(subtrador_inv_1_a), .mult1(Soma_5_out_12), .s1(in_1), .s2(in_2),
    .bit1(out_14), .\null (seletor_4_null));
  validador validador_1 (.s1(in_1), .s2(in_2), .x1(Soma_3_out_13), .x2(or_1_out), .a(error));
  or or_2 (\null , seletor_1_null, seletor_2_null, error, seletor_3_null, seletor_4_null);
endmodule

module seletor (
  input  s1,
  input  s2,
  input  soma1,
  input  sub1,
  input  mult1,
  output bit1,
  output \null 
);

  wire and_2_out, and_3_out, and_4_out, not_1_out, not_2_out, not_3_out, not_4_out;

  not not_1 (not_1_out, s1);
  not not_2 (not_2_out, s2);
  not not_3 (not_3_out, s1);
  not not_4 (not_4_out, s2);
  and and_1 (\null , s1, s2);
  and and_2 (and_2_out, not_1_out, not_2_out, soma1);
  and and_3 (and_3_out, not_3_out, s2, sub1);
  and and_4 (and_4_out, s1, not_4_out, mult1);
  or or_1 (bit1, and_2_out, and_3_out, and_4_out);
endmodule

module subtrador (
  input  x1,
  input  x2,
  input  x3,
  input  x4,
  output a,
  output b,
  output c,
  output d
);

  wire and_1_out, and_2_out, and_3_out, and_4_out, and_5_out, and_6_out, and_7_out, and_8_out, and_9_out,
       not_1_out, not_2_out, not_3_out, not_4_out, not_5_out, not_6_out, not_7_out, not_8_out, not_9_out,
       not_10_out, not_11_out, not_12_out;

  not not_1 (not_1_out, x1);
  not not_2 (not_2_out, x1);
  not not_3 (not_3_out, x1);
  not not_4 (not_4_out, x2);
  not not_5 (not_5_out, x3);
  not not_6 (not_6_out, x4);
  not not_7 (not_7_out, x2);
  and and_1 (and_1_out, not_7_out, x4);
  not not_8 (not_8_out, x2);
  and and_2 (and_2_out, not_8_out, x3);
  and and_3 (and_3_out, x2, not_9_out, not_10_out);
  not not_9 (not_9_out, x3);
  not not_10 (not_10_out, x4);
  not not_11 (not_11_out, x3);
  and and_4 (and_4_out, not_11_out, x4);
  and and_5 (and_5_out, x3, not_12_out);
  not not_12 (not_12_out, x4);
  and and_6 (and_6_out, not_1_out, x4);
  and and_7 (and_7_out, not_2_out, x3);
  and and_8 (and_8_out, not_3_out, x2);
  and and_9 (and_9_out, x1, not_4_out, not_5_out, not_6_out);
  or or_1 (c, and_1_out, and_2_out, and_3_out);
  or or_2 (b, and_4_out, and_5_out);
  or or_3 (d, and_6_out, and_7_out, and_8_out, and_9_out);

  assign a = x4;
endmodule

module multiplicador_um (
  input  x1,
  input  x2,
  input  x3,
  input  x4,
  input  x5,
  output a,
  output b,
  output c,
  output d
);

  wire and_4_out, and_5_out, and_6_out, not_1_out;

  not not_1 (not_1_out, x5);
  and and_1 (c, x1, x3);
  and and_2 (b, x1, x4);
  and and_3 (a, x1, x5);
  and and_4 (and_4_out, x1, x2, not_1_out);
  and and_5 (and_5_out, x1, x2, x4);
  and and_6 (and_6_out, x1, x2, x3);
  or or_1 (d, and_4_out, and_5_out, and_6_out);
endmodule

module multiplicador_dois (
  input  x1,
  input  x2,
  input  x3,
  input  x4,
  input  x5,
  output a,
  output b,
  output c,
  output d,
  output \null 
);

  wire and_3_out, and_4_out, and_5_out, and_6_out, and_7_out, not_1_out, not_2_out;

  not not_1 (not_1_out, x4);
  and and_1 (c, x1, x4);
  not not_2 (not_2_out, x2);
  and and_2 (\null , x1, x2);
  and and_3 (and_3_out, x1, not_1_out, x5);
  and and_4 (and_4_out, x1, x3, x5);
  and and_5 (and_5_out, x1, x2, x5);
  and and_6 (and_6_out, x1, not_2_out, x4, x5);
  and and_7 (and_7_out, x1, x3);
  or or_1 (b, and_3_out, and_4_out, and_5_out);
  or or_2 (d, and_6_out, and_7_out);

  assign a = 1'b0;
endmodule

module multiplicador_tres (
  input  x1,
  input  x2,
  input  x3,
  input  x4,
  input  x5,
  output a,
  output b,
  output c,
  output d,
  output \null 
);

  wire and_3_out, and_4_out;

  and and_1 (c, x1, x5);
  and and_2 (d, x1, x4);
  and and_3 (and_3_out, x1, x3);
  and and_4 (and_4_out, x1, x2);
  or or_1 (\null , and_3_out, and_4_out);

  assign a = 1'b0;
  assign b = 1'b0;
endmodule

module multiplicador_quatro (
  input  x1,
  input  x2,
  input  x3,
  input  x4,
  input  x5,
  output a,
  output b,
  output c,
  output d,
  output \null 
);

  wire and_2_out, and_3_out, and_4_out;

  and and_1 (d, x1, x5);
  and and_2 (and_2_out, x1, x4);
  and and_3 (and_3_out, x1, x3);
  and and_4 (and_4_out, x1, x2);
  or or_1 (\null , and_2_out, and_3_out, and_4_out);

  assign a = 1'b0;
  assign b = 1'b0;
  assign c = 1'b0;
endmodule

module comparador (
  input  x1,
  input  x2,
  input  x3,
  input  x4,
  input  x5,
  output a,
  output b,
  output c
);

  wire and_1_out, and_2_out, and_3_out, and_4_out, and_6_out, and_7_out, and_8_out, and_9_out, not_1_out,
       not_2_out, not_3_out, not_4_out, not_5_out, not_6_out, not_7_out, not_8_out;

  and and_1 (and_1_out, x1, x5);
  and and_2 (and_2_out, x1, x4);
  and and_3 (and_3_out, x1, x3);
  and and_4 (and_4_out, x1, x2);
  not not_1 (not_1_out, x2);
  not not_2 (not_2_out, x3);
  not not_3 (not_3_out, x4);
  not not_4 (not_4_out, x5);
  not not_5 (not_5_out, x1);
  not not_6 (not_6_out, x1);
  not not_7 (not_7_out, x1);
  not not_8 (not_8_out, x1);
  or or_1 (a, and_1_out, and_2_out, and_3_out, and_4_out);
  and and_5 (b, not_1_out, not_2_out, not_3_out, not_4_out);
  and and_6 (and_6_out, not_5_out, x5);
  and and_7 (and_7_out, not_6_out, x4);
  and and_8 (and_8_out, not_7_out, x3);
  and and_9 (and_9_out, not_8_out, x2);
  or or_2 (c, and_6_out, and_7_out, and_8_out, and_9_out);
endmodule

module comparador_erro (
  input  \null ,
  input  x1MAx2,
  input  x1IGUx2,
  input  x1MEx2,
  output x1MAx2_2,
  output x1IGUx2_2,
  output x1MEx2_2
);

  wire not_1_out, not_2_out, not_3_out;

  not not_1 (not_1_out, \null );
  not not_2 (not_2_out, \null );
  not not_3 (not_3_out, \null );
  and and_1 (x1MAx2_2, not_1_out, x1MAx2);
  and and_2 (x1IGUx2_2, not_2_out, x1IGUx2);
  and and_3 (x1MEx2_2, not_3_out, x1MEx2);
endmodule

module subtrador_inv (
  input  cond,
  input  x1,
  input  x2,
  input  x3,
  input  x4,
  output neg,
  output a,
  output b,
  output c,
  output d
);

  wire and_1_out, and_2_out, and_3_out, and_4_out, and_5_out, and_6_out, and_7_out, and_8_out, and_9_out,
       and_10_out, and_11_out, and_12_out, not_1_out, not_2_out, not_3_out, not_4_out, not_5_out, not_6_out,
       not_7_out, not_8_out, not_9_out, not_10_out, not_11_out, not_12_out, not_13_out, not_14_out,
       not_15_out;

  not not_1 (not_1_out, cond);
  not not_2 (not_2_out, x2);
  not not_3 (not_3_out, x3);
  not not_4 (not_4_out, x4);
  not not_5 (not_5_out, x1);
  not not_6 (not_6_out, x1);
  not not_7 (not_7_out, x1);
  not not_8 (not_8_out, cond);
  not not_9 (not_9_out, x3);
  not not_10 (not_10_out, x4);
  not not_11 (not_11_out, x2);
  not not_12 (not_12_out, x2);
  not not_13 (not_13_out, cond);
  not not_14 (not_14_out, x4);
  not not_15 (not_15_out, x3);
  and and_1 (and_1_out, not_1_out, x1);
  and and_2 (and_2_out, x1, not_2_out, not_3_out, not_4_out);
  and and_3 (and_3_out, cond, not_5_out, x4);
  and and_4 (and_4_out, cond, not_6_out, x3);
  and and_5 (and_5_out, cond, not_7_out, x2);
  and and_6 (and_6_out, not_8_out, x2);
  and and_7 (and_7_out, x2, not_9_out, not_10_out);
  and and_8 (and_8_out, cond, not_11_out, x4);
  and and_9 (and_9_out, cond, not_12_out, x3);
  and and_10 (and_10_out, not_13_out, x3);
  and and_11 (and_11_out, x3, not_14_out);
  and and_12 (and_12_out, cond, not_15_out, x4);
  or or_1 (a, and_1_out, and_2_out, and_3_out, and_4_out, and_5_out);
  or or_2 (b, and_6_out, and_7_out, and_8_out, and_9_out);
  or or_3 (c, and_10_out, and_11_out, and_12_out);

  assign d = x4;
  assign neg = cond;
endmodule

module validador (
  input  s1,
  input  s2,
  input  x1,
  input  x2,
  output a
);

  wire and_1_out, and_2_out, not_1_out, not_2_out, not_3_out;

  not not_1 (not_1_out, s1);
  and and_1 (and_1_out, not_1_out, not_2_out, x1);
  not not_2 (not_2_out, s2);
  and and_2 (and_2_out, s1, not_3_out, x2);
  not not_3 (not_3_out, s2);
  or or_1 (a, and_1_out, and_2_out);
endmodule
